// Logisim project ETFExtended.circ as structural Verilog: 8 circuits, main circuit INTERRUPT_INTERFACE_4
module INTERRUPT_INTERFACE_4 (
  input  BTN_INTR0,
  input  BTN_INTR1,
  input  BTN_INTR2,
  input  BTN_INTR3,
  input  inta,
  input  [1:0] UEXT1__0,
  input  CLK,
  output [3:0] intr3__0
);

  wire and_1_out, and_2_out, and_3_out, and_4_out, D0, D1, D2, D3;

  // DC2_4 dc2_4_1: pin names not known; wires that end beside it: UEXT1__0, inta, D0, D1, D2, D3
  and and_1 (and_1_out, D0, ~BTN_INTR0);  // AND_Gate
  and and_2 (and_2_out, D1, ~BTN_INTR1);  // AND_Gate
  and and_3 (and_3_out, D2, ~BTN_INTR2);  // AND_Gate
  and and_4 (and_4_out, D3, ~BTN_INTR3);  // AND_Gate
  // RSFF rsff_1: pin names not known; wires that end beside it: and_1_out, CLK, BTN_INTR0, intr3__0[0]
  // RSFF rsff_2: pin names not known; wires that end beside it: and_2_out, CLK, BTN_INTR1, intr3__0[1]
  // RSFF rsff_3: pin names not known; wires that end beside it: and_3_out, CLK, BTN_INTR2, intr3__0[2]
  // RSFF rsff_4: pin names not known; wires that end beside it: and_4_out, CLK, BTN_INTR3, intr3__0[3]

  // Other names for the same wires on the sheet: intr0 = intr3__0[0]; intr1 = intr3__0[1]; intr2 = intr3__0[2];
  //   intr3 = intr3__0[3]
endmodule

module INTERRUPT_INTERFACE_8 (
  input  BTN_INTR0,
  input  BTN_INTR1,
  input  BTN_INTR2,
  input  BTN_INTR3,
  input  BTN_INTR4,
  input  BTN_INTR5,
  input  BTN_INTR6,
  input  BTN_INTR7,
  input  inta,
  input  [2:0] UEXT2__0,
  input  CLK,
  output [7:0] intr7__0
);

  wire and_1_out, and_2_out, and_3_out, and_4_out, and_5_out, and_6_out, and_7_out, and_8_out, D0, D1, D2,
       D3, D4, D5, D6, D7;

  // DC3_8 dc3_8_1: pin names not known; wires that end beside it: UEXT2__0, inta, D0, D1, D2, D3, D4, D5, D6, D7
  and and_1 (and_1_out, D0, ~BTN_INTR0);  // AND_Gate
  and and_2 (and_2_out, D1, ~BTN_INTR1);  // AND_Gate
  and and_3 (and_3_out, D2, ~BTN_INTR2);  // AND_Gate
  and and_4 (and_4_out, D3, ~BTN_INTR3);  // AND_Gate
  and and_5 (and_5_out, D4, ~BTN_INTR4);  // AND_Gate
  and and_6 (and_6_out, D5, ~BTN_INTR5);  // AND_Gate
  and and_7 (and_7_out, D6, ~BTN_INTR6);  // AND_Gate
  and and_8 (and_8_out, D7, ~BTN_INTR7);  // AND_Gate
  // RSFF rsff_1: pin names not known; wires that end beside it: and_1_out, CLK, BTN_INTR0, intr7__0[0]
  // RSFF rsff_2: pin names not known; wires that end beside it: and_2_out, CLK, BTN_INTR1, intr7__0[1]
  // RSFF rsff_3: pin names not known; wires that end beside it: and_3_out, CLK, BTN_INTR2, intr7__0[2]
  // RSFF rsff_4: pin names not known; wires that end beside it: and_4_out, CLK, BTN_INTR3, intr7__0[3]
  // RSFF rsff_5: pin names not known; wires that end beside it: and_5_out, CLK, BTN_INTR4, intr7__0[4]
  // RSFF rsff_6: pin names not known; wires that end beside it: and_6_out, CLK, BTN_INTR5, intr7__0[5]
  // RSFF rsff_7: pin names not known; wires that end beside it: and_7_out, CLK, BTN_INTR6, intr7__0[6]
  // RSFF rsff_8: pin names not known; wires that end beside it: and_8_out, CLK, BTN_INTR7, intr7__0[7]

  // Other names for the same wires on the sheet: intr0 = intr7__0[0]; intr1 = intr7__0[1]; intr2 = intr7__0[2];
  //   intr3 = intr7__0[3]; intr4 = intr7__0[4]; intr5 = intr7__0[5]; intr6 = intr7__0[6]; intr7 = intr7__0[7]
endmodule

module ROM16x17 (
  input  [3:0] A3__0,
  input  CS,
  output [16:0] DOUT
);

  ROM #(.addrWidth(4), .dataWidth(17)) rom_1 (.addr(A3__0), .data(DOUT), .sel(CS));
endmodule

module ROM16x24 (
  input  [3:0] A3__0,
  input  CS,
  output [23:0] DOUT
);

  ROM #(.addrWidth(4), .dataWidth(24)) rom_1 (.addr(A3__0), .data(DOUT), .sel(CS));
endmodule

module ROM16x26 (
  input  [3:0] A3__0,
  input  CS,
  output [25:0] DOUT
);

  ROM #(.addrWidth(4), .dataWidth(26)) rom_1 (.addr(A3__0), .data(DOUT), .sel(CS));
endmodule

module ROM64x37 (
  input  [5:0] A5__0,
  input  CS,
  output [30:0] DOUT30__0,
  output [5:0] DOUT36__31
);

  ROM #(.addrWidth(6), .dataWidth(6)) rom_1 (.addr(A5__0), .data(DOUT36__31), .sel(CS));
  ROM #(.addrWidth(6), .dataWidth(31)) rom_2 (.addr(A5__0), .data(DOUT30__0), .sel(CS));
endmodule

module GPR8x16 (
  input  [15:0] DI15__0,
  input  [3:0] A3__0,
  input  WR,
  input  CLK,
  input  RST,
  input  [15:0] in_6,
  input  [15:0] in_7,
  input  in_8,
  input  in_9,
  input  in_10,
  input  in_11,
  input  in_12,
  input  in_13,
  output [15:0] DO15__0,
  output [15:0] out_15,
  output [15:0] OUTSP15__0,
  output [15:0] OUTPC15__0
);

  wire and_2_out, and_3_out, and_5_out, and_7_out, and_8_out, CS0, CS1, CS2, CS3, CS4, CS5, CS6, CS7, CS8,
       CS9, CS10, CS11, CS12, CS13, CS14, CS15, mp2_16b_1_p3, reg16_3_p4, reg16_ld_1_p4, reg16_ld_4_p4,
       reg16_ld_6_p4, reg16_ld_9_p4, reg16_ld_10_p4, reg16_ld_11_p4, reg16_ld_12_p4, reg16_ld_13_p4;
  wire [15:0] reg16_ld_1_p3, reg16_ld_2_p3, reg16_ld_3_p3, reg16_ld_4_p3, reg16_ld_5_p3, reg16_ld_6_p3,
       reg16_ld_7_p3, reg16_ld_8_p3, reg16_ld_9_p3, reg16_ld_10_p3, reg16_ld_11_p3, reg16_ld_12_p3,
       reg16_ld_13_p3;

  // DC4_16 dc4_16_1: pin names not known; wires that end beside it: A3__0, 1'b1, CS0, CS1, CS2, CS3, CS4, CS5, CS6, CS7, CS8, CS9, CS10, CS11, CS12, CS13, CS14, CS15
  // REG16 reg16_1: pin names not known; wires that end beside it: CLK, 16'hf000, OUTSP15__0, RST, in_11, in_10
  // REG16 reg16_2: pin names not known; wires that end beside it: RST, CLK, in_6, out_15, in_8, in_9, out_15[15]
  // MP2_16b mp2_16b_1: pin names not known; wires that end beside it: RST, in_7, mp2_16b_1_p3, 16'h1000, 1'b1
  // REG16 reg16_3: pin names not known; wires that end beside it: CLK, mp2_16b_1_p3, OUTPC15__0, reg16_3_p4, in_13
  or or_1 (reg16_3_p4, in_12, RST);
  // REG16_LD reg16_ld_1: pin names not known; wires that end beside it: CLK, DI15__0, reg16_ld_1_p3, reg16_ld_1_p4
  and and_1 (reg16_ld_1_p4, CS5, WR);
  assign DO15__0 = CS5 ? reg16_ld_1_p3 : 16'bz;  // Controlled_Buffer controlled_buffer_1
  and and_2 (and_2_out, CS6, WR);
  // REG16_LD reg16_ld_2: pin names not known; wires that end beside it: CLK, DI15__0, reg16_ld_2_p3, and_2_out
  assign DO15__0 = CS6 ? reg16_ld_2_p3 : 16'bz;  // Controlled_Buffer controlled_buffer_2
  and and_3 (and_3_out, CS7, WR);
  // REG16_LD reg16_ld_3: pin names not known; wires that end beside it: CLK, DI15__0, reg16_ld_3_p3, and_3_out
  assign DO15__0 = CS7 ? reg16_ld_3_p3 : 16'bz;  // Controlled_Buffer controlled_buffer_3
  // REG16_LD reg16_ld_4: pin names not known; wires that end beside it: CLK, DI15__0, reg16_ld_4_p3, reg16_ld_4_p4
  assign DO15__0 = CS3 ? reg16_ld_4_p3 : 16'bz;  // Controlled_Buffer controlled_buffer_4
  and and_4 (reg16_ld_4_p4, CS3, WR);
  and and_5 (and_5_out, CS4, WR);
  // REG16_LD reg16_ld_5: pin names not known; wires that end beside it: CLK, DI15__0, reg16_ld_5_p3, and_5_out
  assign DO15__0 = CS4 ? reg16_ld_5_p3 : 16'bz;  // Controlled_Buffer controlled_buffer_5
  // REG16_LD reg16_ld_6: pin names not known; wires that end beside it: CLK, DI15__0, reg16_ld_6_p3, reg16_ld_6_p4
  and and_6 (reg16_ld_6_p4, CS8, WR);
  assign DO15__0 = CS8 ? reg16_ld_6_p3 : 16'bz;  // Controlled_Buffer controlled_buffer_6
  and and_7 (and_7_out, CS9, WR);
  // REG16_LD reg16_ld_7: pin names not known; wires that end beside it: CLK, DI15__0, reg16_ld_7_p3, and_7_out
  assign DO15__0 = CS9 ? reg16_ld_7_p3 : 16'bz;  // Controlled_Buffer controlled_buffer_7
  and and_8 (and_8_out, CS10, WR);
  // REG16_LD reg16_ld_8: pin names not known; wires that end beside it: CLK, DI15__0, reg16_ld_8_p3, and_8_out
  assign DO15__0 = CS10 ? reg16_ld_8_p3 : 16'bz;  // Controlled_Buffer controlled_buffer_8
  // REG16_LD reg16_ld_9: pin names not known; wires that end beside it: CLK, DI15__0, reg16_ld_9_p3, reg16_ld_9_p4
  and and_9 (reg16_ld_9_p4, CS11, WR);
  assign DO15__0 = CS11 ? reg16_ld_9_p3 : 16'bz;  // Controlled_Buffer controlled_buffer_9
  // REG16_LD reg16_ld_10: pin names not known; wires that end beside it: CLK, DI15__0, reg16_ld_10_p3, reg16_ld_10_p4
  assign DO15__0 = CS12 ? reg16_ld_10_p3 : 16'bz;  // Controlled_Buffer controlled_buffer_10
  // REG16_LD reg16_ld_11: pin names not known; wires that end beside it: CLK, DI15__0, reg16_ld_11_p3, reg16_ld_11_p4
  assign DO15__0 = CS13 ? reg16_ld_11_p3 : 16'bz;  // Controlled_Buffer controlled_buffer_11
  // REG16_LD reg16_ld_12: pin names not known; wires that end beside it: CLK, DI15__0, reg16_ld_12_p3, reg16_ld_12_p4
  assign DO15__0 = CS14 ? reg16_ld_12_p3 : 16'bz;  // Controlled_Buffer controlled_buffer_12
  // REG16_LD reg16_ld_13: pin names not known; wires that end beside it: CLK, DI15__0, reg16_ld_13_p3, reg16_ld_13_p4
  assign DO15__0 = CS15 ? reg16_ld_13_p3 : 16'bz;  // Controlled_Buffer controlled_buffer_13
  and and_10 (reg16_ld_10_p4, CS12, WR);
  and and_11 (reg16_ld_11_p4, CS13, WR);
  and and_12 (reg16_ld_12_p4, CS14, WR);
  and and_13 (reg16_ld_13_p4, CS15, WR);

  // Other names for the same wires on the sheet: decsp = in_10; INACC15__0[15:0] = in_6; incpc = in_13; incsp = in_11;
  //   INPC15__0[15:0] = in_7; inREG[15:0] = DI15__0; LDA = in_8; ldpc = in_12; AB15 = out_15[15];
  //   outREG[15:0] = DO15__0; SLA = in_9
endmodule

module MP2_6b (
  input  En,
  input  [5:0] _5__0,
  input  [5:0] in_3,
  input  S0,
  output [5:0] Y
);

  wire not_1_out;
  wire [5:0] and_1_out, and_2_out, bit_extender_1_out, bit_extender_2_out, bit_extender_3_out, or_1_out;

  Pull_Resistor #(.pull(1)) pull_resistor_1 (.node(En));
  assign bit_extender_1_out = {{5{S0}}, S0};  // Bit_Extender bit_extender_1
  not not_1 (not_1_out, S0);
  assign bit_extender_2_out = {{5{not_1_out}}, not_1_out};  // Bit_Extender bit_extender_2
  assign and_1_out = _5__0 & bit_extender_2_out;  // AND_Gate and_1, 6 bits wide
  assign and_2_out = in_3 & bit_extender_1_out;  // AND_Gate and_2, 6 bits wide
  assign bit_extender_3_out = {{5{En}}, En};  // Bit_Extender bit_extender_3
  assign or_1_out = and_1_out | and_2_out;  // OR_Gate or_1, 6 bits wide
  assign Y = bit_extender_3_out & or_1_out;  // AND_Gate and_3, 6 bits wide

  // Notes on the sheet:
  //   I0
  //   I1
  //   5..0
  //   Ako En nije priključen (stanje visoke impednase - HiZ),
  //   uezti za podrazumevanu vrednost logičku jedinicu
  //   5..0
endmodule
