// Logisim project ETFStudent.circ as structural Verilog: 5 circuits, main circuit REG32_LD
module REG32_LD (
  input  [31:0] I15__0,
  input  LD,
  input  mr,
  input  CLK,
  output [31:0] A15__0
);

  // REG16_LD reg16_ld_1: pin names not known; wires that end beside it: CLK, mr, I15__0[31:16], A15__0[31:16], LD
  // REG16_LD reg16_ld_2: pin names not known; wires that end beside it: CLK, mr, I15__0[15:0], A15__0[15:0], LD

  // Notes on the sheet:
  //   __
endmodule

module KMADR (
  input  immed,
  input  memdir,
  input  regdir,
  input  regindpom,
  output [3:0] Adr3__0
);

  assign Adr3__0 = immed ? 4'b0010 : 4'bz;  // Controlled_Buffer controlled_buffer_1
  assign Adr3__0 = memdir ? 4'b0100 : 4'bz;  // Controlled_Buffer controlled_buffer_2
  assign Adr3__0 = regdir ? 4'b0101 : 4'bz;  // Controlled_Buffer controlled_buffer_3
  assign Adr3__0 = regindpom ? 4'b0111 : 4'bz;  // Controlled_Buffer controlled_buffer_4
endmodule

module KMOPR (
  input  LD,
  input  ST,
  input  ADD,
  input  SUB,
  input  BLSS,
  input  JLEQ,
  input  JMP,
  input  JSR,
  input  RTS,
  input  RTI,
  input  HALT,
  output [5:0] Adr5__0
);

  assign Adr5__0 = LD ? 6'b000010 : 6'bz;  // Controlled_Buffer controlled_buffer_1
  assign Adr5__0 = ST ? 6'b000100 : 6'bz;  // Controlled_Buffer controlled_buffer_2
  assign Adr5__0 = ADD ? 6'b001010 : 6'bz;  // Controlled_Buffer controlled_buffer_3
  assign Adr5__0 = SUB ? 6'b001100 : 6'bz;  // Controlled_Buffer controlled_buffer_4
  assign Adr5__0 = BLSS ? 6'b001110 : 6'bz;  // Controlled_Buffer controlled_buffer_5
  assign Adr5__0 = JLEQ ? 6'b010000 : 6'bz;  // Controlled_Buffer controlled_buffer_6
  assign Adr5__0 = JMP ? 6'b010001 : 6'bz;  // Controlled_Buffer controlled_buffer_7
  assign Adr5__0 = JSR ? 6'b010010 : 6'bz;  // Controlled_Buffer controlled_buffer_8
  assign Adr5__0 = RTS ? 6'b010111 : 6'bz;  // Controlled_Buffer controlled_buffer_9
  assign Adr5__0 = RTI ? 6'b011110 : 6'bz;  // Controlled_Buffer controlled_buffer_10
  assign Adr5__0 = HALT ? 6'b100010 : 6'bz;  // Controlled_Buffer controlled_buffer_11
endmodule

module REG6_INC_LD (
  input  [5:0] I5__0,
  input  LD,
  input  INC,
  input  mr,
  input  CLK,
  output [5:0] A5__0
);

  wire reg2m_inc_ld_1_p7, reg2m_inc_ld_2_p8;

  // REG2m_INC_LD reg2m_inc_ld_1: pin names not known; wires that end beside it: CLK, mr, I5__0[5:4], A5__0[5:4], LD, INC, reg2m_inc_ld_1_p7
  // REG2m_INC_LD reg2m_inc_ld_2: pin names not known; wires that end beside it: CLK, reg2m_inc_ld_1_p7, mr, I5__0[3:2], A5__0[3:2], LD, INC, reg2m_inc_ld_2_p8
  // REG2m_INC_LD reg2m_inc_ld_3: pin names not known; wires that end beside it: CLK, reg2m_inc_ld_2_p8, mr, I5__0[1:0], A5__0[1:0], LD, INC, INC

  // Notes on the sheet:
  //   __
endmodule

module ALU16 (
  input  [15:0] A15__0,
  input  [15:0] B15__0,
  input  ADD,
  input  MUL,
  input  DEC,
  input  NOT,
  output [15:0] ALU15__0,
  output ALU16
);

  wire add16_1_p1, sub16_1_p1;
  wire [15:0] add16_1_p3, multiplier_1_out, negator_1_out, sub16_1_p3;

  assign ALU16 = DEC ? sub16_1_p1 : 1'bz;  // Controlled_Buffer controlled_buffer_1
  // SUB16 sub16_1: pin names not known; wires that end beside it: sub16_1_p1, A15__0, sub16_1_p3, 16'h1, 1'b0
  assign ALU15__0 = DEC ? sub16_1_p3 : 16'bz;  // Controlled_Buffer controlled_buffer_2
  assign ALU16 = ADD ? add16_1_p1 : 1'bz;  // Controlled_Buffer controlled_buffer_3
  // ADD16 add16_1: pin names not known; wires that end beside it: add16_1_p1, A15__0, add16_1_p3, B15__0, 1'b0
  assign ALU15__0 = ADD ? add16_1_p3 : 16'bz;  // Controlled_Buffer controlled_buffer_4
  Negator #(.width(16)) negator_1 (.in(A15__0), .out(negator_1_out));
  assign ALU15__0 = NOT ? negator_1_out : 16'bz;  // Controlled_Buffer controlled_buffer_5
  Multiplier multiplier_1 (
    .a(B15__0[7:0]), .b(A15__0[7:0]), .out(multiplier_1_out[7:0]), .cout(multiplier_1_out[15:8]));  // open: cin
  assign ALU15__0 = MUL ? multiplier_1_out : 16'bz;  // Controlled_Buffer controlled_buffer_6
endmodule
