// Logisim project ORT2Project.circ as structural Verilog: 8 circuits, main circuit COMPUTER
module COMPUTER (
);

  wire BTN_INTR0_out, BTN_INTR1_out, BTN_INTR2_out, BTN_INTR3_out, BTN_INTR4_out, BTN_INTR5_out,
       BTN_INTR6_out, BTN_INTR7_out, BTN_RST_out, CLK, cpu_1_inta, pull_resistor_4_node,
       pull_resistor_6_node, ram_1_out_8, rst;
  wire [2:0] cpu_1_uext2__0;
  wire [7:0] interrupt_interface_8_1_intr7__0, pull_resistor_3_node, ram_1_out_7;
  wire [15:0] pull_resistor_1_node;

  Button BTN_RST (.out(BTN_RST_out));
  Clock u_CLK (.out(CLK));
  // RisingEdge risingedge_1: pin names not known; wires that end beside it: BTN_RST_out, CLK, rst
  RAM ram_1 (
    .in_1(pull_resistor_1_node), .in_2(CLK), .in_3(pull_resistor_3_node), .in_4(pull_resistor_4_node),
    .in_5(pull_resistor_6_node), .in_6(rst), .out_7(ram_1_out_7), .out_8(ram_1_out_8));
  Pull_Resistor pull_resistor_1 (.node(pull_resistor_1_node));
  Pull_Resistor pull_resistor_2 (.node(ram_1_out_7));
  Pull_Resistor pull_resistor_3 (.node(pull_resistor_3_node));
  Pull_Resistor pull_resistor_4 (.node(pull_resistor_4_node));
  Pull_Resistor pull_resistor_5 (.node(ram_1_out_8));
  Pull_Resistor pull_resistor_6 (.node(pull_resistor_6_node));
  CPU cpu_1 (
    .in_1(rst), .in_2(CLK), .in_3(ram_1_out_8), .in_4(ram_1_out_7), .ABUS(pull_resistor_1_node),
    .DOUTBUS(pull_resistor_3_node), .out_8(pull_resistor_4_node), .out_9(pull_resistor_6_node),
    .inta(cpu_1_inta), .intr7__0(interrupt_interface_8_1_intr7__0), .UEXT2__0(cpu_1_uext2__0));
  INTERRUPT_INTERFACE_8 interrupt_interface_8_1 (
    .BTN_INTR0(BTN_INTR0_out), .BTN_INTR1(BTN_INTR1_out), .BTN_INTR2(BTN_INTR2_out),
    .BTN_INTR3(BTN_INTR3_out), .BTN_INTR4(BTN_INTR4_out), .BTN_INTR5(BTN_INTR5_out),
    .BTN_INTR6(BTN_INTR6_out), .BTN_INTR7(BTN_INTR7_out), .inta(cpu_1_inta), .UEXT2__0(cpu_1_uext2__0),
    .CLK(CLK), .intr7__0(interrupt_interface_8_1_intr7__0));
  Button BTN_INTR7 (.out(BTN_INTR7_out));
  Button BTN_INTR6 (.out(BTN_INTR6_out));
  Button BTN_INTR5 (.out(BTN_INTR5_out));
  Button BTN_INTR4 (.out(BTN_INTR4_out));
  Button BTN_INTR3 (.out(BTN_INTR3_out));
  Button BTN_INTR2 (.out(BTN_INTR2_out));
  Button BTN_INTR1 (.out(BTN_INTR1_out));
  Button BTN_INTR0 (.out(BTN_INTR0_out));
endmodule

module CPU (
  input  in_1,
  input  in_2,
  input  in_3,
  input  [7:0] in_4,
  input  [7:0] intr7__0,
  output [15:0] ABUS,
  output [7:0] DOUTBUS,
  output out_8,
  output out_9,
  output inta,
  output [2:0] UEXT2__0
);

  wire [3:0] common_1_phaseffbus, intr3__0;
  wire [6:0] common_1_addrbus;
  wire [7:0] pull_resistor_4_node;
  wire [8:0] pull_resistor_1_node;
  wire [14:0] pull_resistor_5_node;
  wire [15:0] A, ALU, B, INTRADDR, PSW;
  wire [16:0] pull_resistor_7_node;
  wire [21:0] common_1_instrucbus;

  COMMON common_1 (
    .CLK(in_2), .RST(in_1), .DIN(in_4), .CMEMBUS(pull_resistor_5_node), .MAR(ABUS), .MDR(DOUTBUS),
    .PHASEFFBUS(common_1_phaseffbus), .INSTRUCBUS(common_1_instrucbus), .ADDRBUS(common_1_addrbus),
    .PSW(PSW), .CREGBUS(pull_resistor_7_node), .CFFBUS(pull_resistor_4_node), .B(B), .A(A),
    .CPSW(pull_resistor_1_node), .ALU(ALU), .IVTPPDSP(INTRADDR));
  Pull_Resistor pull_resistor_1 (.node(pull_resistor_1_node));
  Pull_Resistor pull_resistor_2 (.node(common_1_phaseffbus));
  Pull_Resistor pull_resistor_3 (.node(common_1_instrucbus));
  Pull_Resistor pull_resistor_4 (.node(pull_resistor_4_node));
  Pull_Resistor pull_resistor_5 (.node(pull_resistor_5_node));
  Pull_Resistor pull_resistor_6 (.node(common_1_addrbus));
  Pull_Resistor pull_resistor_7 (.node(pull_resistor_7_node));
  FETCH fetch_1 (
    .in_1(in_1), .in_2(in_2), .in_3(in_3), .PHASEFFBUS(common_1_phaseffbus),
    .INSTRUCBUS(common_1_instrucbus), .ADDRBUS(common_1_addrbus), .PSW(PSW), .rdMEM(out_9),
    .CMEMBUS(pull_resistor_5_node), .CFFBUS(pull_resistor_4_node), .CREGBUS(pull_resistor_7_node));
  ADDR addr_1 (
    .in_1(in_1), .in_2(in_2), .in_3(in_3), .PHASEFFBUS(common_1_phaseffbus),
    .INSTRUCBUS(common_1_instrucbus), .ADDRBUS(common_1_addrbus), .rdMEM(out_9),
    .CMEMBUS(pull_resistor_5_node), .CFFBUS(pull_resistor_4_node), .CREGBUS(pull_resistor_7_node));
  EXEC exec_1 (
    .in_2(in_1), .in_3(in_2), .in_4(in_3), .B(B), .PHASEFFBUS(common_1_phaseffbus),
    .INSTRUCBUS(common_1_instrucbus), .ADDRBUS(common_1_addrbus), .PSW(PSW), .A(A), .ALU(ALU),
    .CMEMBUS(pull_resistor_5_node), .CFFBUS(pull_resistor_4_node), .CREGBUS(pull_resistor_7_node),
    .CPSW(pull_resistor_1_node[6:0]), .rdMEM(out_9), .wrMEM(out_8));
  INTR intr_1 (
    .in_1(in_1), .in_2(in_2), .in_3(in_3), .PHASEFFBUS(common_1_phaseffbus),
    .INSTRUCBUS(common_1_instrucbus), .PSW(PSW), .intr(intr3__0), .ADDIVTP(INTRADDR),
    .CMEMBUS(pull_resistor_5_node), .CFFBUS(pull_resistor_4_node), .CREGBUS(pull_resistor_7_node),
    .rdMEM(out_9), .wrMEM(out_8), .UEXT1__0(UEXT2__0), .inta(inta));
  // Pins of 7 and 9 bits meet at pull_resistor_1_node

  // Other names for the same wires on the sheet: CLK = in_2; DIN7__0[7:0] = in_4; FCBUS = in_3; MAR[15:0] = ABUS;
  //   MDR[7:0] = DOUTBUS; RD = out_9; rst = in_1; WR = out_8
endmodule

module COMMON (
  input  CLK,
  input  RST,
  input  [7:0] DIN,
  input  [15:0] ALU,
  input  [15:0] IVTPPDSP,
  input  [14:0] CMEMBUS,
  input  [7:0] CFFBUS,
  input  [16:0] CREGBUS,
  input  [8:0] CPSW,
  output [15:0] MAR,
  output [7:0] MDR,
  output [15:0] A,
  output [3:0] PHASEFFBUS,
  output [21:0] INSTRUCBUS,
  output [6:0] ADDRBUS,
  output [15:0] PSW,
  output [15:0] B
);

  wire ADRINST, adrinst_t, and_1_out, and_2_out, and_3_out, and_4_out, and_12_out, and_13_out, and_14_out,
       and_15_out, and_16_out, and_17_out, and_18_out, and_19_out, and_20_out, and_21_out, and_22_out,
       and_23_out, and_24_out, and_25_out, and_26_out, and_27_out, and_28_out, and_29_out, and_30_out,
       and_31_out, and_32_out, and_33_out, and_34_out, and_35_out, and_36_out, and_37_out, and_38_out,
       bezadrinst, branchinst, dc3_8_4_p3, dc3_8_4_p4, dc3_8_4_p5, dc3_8_4_p6, dc3_8_4_p7, dc3_8_4_p8,
       dc3_8_4_p9, greska, INSTR, jmpinstr, mp4_16b_1_p5, mp8_8b_1_p8, mp8_16b_1_p8, not_1_out, not_4_out,
       not_10_out, or_2_out, or_3_out, or_4_out, or_5_out, or_6_out, or_7_out, or_8_out, or_9_out, or_10_out,
       or_11_out, rsff_2_p4, rsff_3_p4, rsff_6_p4, rsff_7_p4, rsff_9_p4;
  wire [3:0] IR19__16, IR27__24;
  wire [5:4] IR29__24;
  wire [7:0] DW7__0, IR7__0, IR15__8, PC7__0;
  wire [7:4] IR23__16;
  wire [7:6] IR31__24;
  wire [15:0] addMAR, addrPC, mp2_16b_1_p3, mp4_16b_2_p5, mp4_16b_3_p5, outGPR, SP15__0;
  wire [15:8] DW15__0, PC15__0;

  // REG8_LD reg8_ld_1: pin names not known; wires that end beside it: CLK, MDR, {IR31__24, IR29__24, IR27__24}, CREGBUS[7]
  // MP8_16b mp8_16b_1: pin names not known; wires that end beside it: CMEMBUS[7], CMEMBUS[6], CMEMBUS[5], {PC15__0, PC7__0}, {IR15__8, IR7__0}, {DW15__0, DW7__0}, outGPR, mp8_16b_1_p8, B, addMAR, SP15__0, IVTPPDSP, 1'b1
  // REG16_INC_LD reg16_inc_ld_1: pin names not known; wires that end beside it: CLK, mp8_16b_1_p8, MAR, CMEMBUS[0], CMEMBUS[1]
  // REG8_LD reg8_ld_2: pin names not known; wires that end beside it: CLK, MDR, {IR23__16, IR19__16}, CREGBUS[6]
  // REG8_LD reg8_ld_3: pin names not known; wires that end beside it: CLK, MDR, DW15__0, CREGBUS[15]
  and and_1 (and_1_out, bezadrinst, ~IR27__24[3]);  // AND_Gate
  and and_2 (and_2_out, branchinst, ~IR27__24[3]);  // AND_Gate
  // DC2_4 dc2_4_1: pin names not known; wires that end beside it: IR31__24, PSW[0], INSTR
  // DC2_4 dc2_4_2: pin names not known; wires that end beside it: IR29__24, INSTR, bezadrinst, branchinst, jmpinstr, adrinst_t
  // DC3_8 dc3_8_1: pin names not known; wires that end beside it: IR27__24[2:0], and_1_out, INSTRUCBUS[0], INSTRUCBUS[1], INSTRUCBUS[2], INSTRUCBUS[3], INSTRUCBUS[4], INSTRUCBUS[5], INSTRUCBUS[6], INSTRUCBUS[7]
  // DC3_8 dc3_8_2: pin names not known; wires that end beside it: IR27__24[2:0], and_2_out, INSTRUCBUS[8], INSTRUCBUS[9], INSTRUCBUS[10], INSTRUCBUS[11], INSTRUCBUS[12], INSTRUCBUS[13]
  // ADD16 add16_1: pin names not known; wires that end beside it: outGPR, addMAR, {{9{IR15__8[7]}}, IR15__8[6:0]}
  // REG8_LD reg8_ld_4: pin names not known; wires that end beside it: CLK, MDR, IR15__8, CREGBUS[5]
  // REG8_LD reg8_ld_5: pin names not known; wires that end beside it: CLK, MDR, DW7__0, CREGBUS[14]
  // MP8_8b mp8_8b_1: pin names not known; wires that end beside it: CMEMBUS[10], CMEMBUS[9], CMEMBUS[8], DIN, A[15:8], A[7:0], PC15__0, mp8_8b_1_p8, PC7__0, PSW[15:8], PSW[7:0], 1'b1
  // REG8_LD reg8_ld_6: pin names not known; wires that end beside it: CLK, mp8_8b_1_p8, MDR, CMEMBUS[2]
  and and_3 (and_3_out, jmpinstr, ~IR27__24[2], ~IR27__24[3]);  // AND_Gate
  // REG8_LD reg8_ld_7: pin names not known; wires that end beside it: CLK, MDR, IR7__0, CREGBUS[4]
  // DC2_4 dc2_4_3: pin names not known; wires that end beside it: IR27__24[1:0], and_3_out, INSTRUCBUS[14], INSTRUCBUS[15], INSTRUCBUS[16]
  and and_4 (and_4_out, adrinst_t, ~IR27__24[3]);  // AND_Gate
  or or_1 (greska, IR19__16[3], IR19__16[2], IR23__16[7], IR19__16[1], IR19__16[0]);
  // DC3_8 dc3_8_3: pin names not known; wires that end beside it: IR27__24[2:0], and_4_out, INSTRUCBUS[17], INSTRUCBUS[18], INSTRUCBUS[19], INSTRUCBUS[20], INSTRUCBUS[21]
  // DC3_8 dc3_8_4: pin names not known; wires that end beside it: IR23__16[6:4], adrinst_t, dc3_8_4_p3, dc3_8_4_p4, dc3_8_4_p5, dc3_8_4_p6, dc3_8_4_p7, dc3_8_4_p8, dc3_8_4_p9
  // ADD16 add16_2: pin names not known; wires that end beside it: {PC15__0, PC7__0}, addrPC, {{9{IR23__16[7]}}, IR23__16[6:4], IR19__16}
  // MP4_16b mp4_16b_1: pin names not known; wires that end beside it: CREGBUS[11], CREGBUS[10], {IR15__8, IR7__0}, outGPR, mp4_16b_1_p5, {DW15__0, DW7__0}, 1'b1
  // REG16 reg16_1: pin names not known; wires that end beside it: CLK, mp4_16b_1_p5, B, CREGBUS[8], CREGBUS[9]
  not not_1 (not_1_out, RST);
  // RSFF rsff_1: pin names not known; wires that end beside it: CFFBUS[1], CLK, CFFBUS[0], not_1_out, PHASEFFBUS[0]
  and and_5 (ADDRBUS[6], ~IR23__16[7], dc3_8_4_p9);  // AND_Gate
  and and_6 (ADDRBUS[0], ~greska, dc3_8_4_p3);  // AND_Gate
  and and_7 (ADDRBUS[3], ~IR23__16[7], dc3_8_4_p6);  // AND_Gate
  and and_8 (ADDRBUS[4], ~IR23__16[7], dc3_8_4_p7);  // AND_Gate
  and and_9 (ADDRBUS[5], ~IR23__16[7], dc3_8_4_p8);  // AND_Gate
  and and_10 (ADDRBUS[1], ~greska, dc3_8_4_p4);  // AND_Gate
  and and_11 (ADDRBUS[2], ~greska, dc3_8_4_p5);  // AND_Gate
  // RSFF rsff_2: pin names not known; wires that end beside it: CFFBUS[3], CLK, CFFBUS[2], rsff_2_p4, PHASEFFBUS[1]
  not not_2 (rsff_2_p4, RST);
  // MP2_16b mp2_16b_1: pin names not known; wires that end beside it: CREGBUS[13], B, mp2_16b_1_p3, A, 1'b1
  and and_12 (and_12_out, MDR[1], INSTRUCBUS[2]);
  and and_13 (and_13_out, ADRINST, A[15]);
  and and_14 (and_14_out, INSTRUCBUS[19], CREGBUS[16]);
  and and_15 (and_15_out, INSTRUCBUS[5], A[15]);
  and and_16 (and_16_out, INSTRUCBUS[13], ~CREGBUS[16]);  // AND_Gate
  // RSFF rsff_3: pin names not known; wires that end beside it: CFFBUS[5], CLK, CFFBUS[4], rsff_3_p4, PHASEFFBUS[2]
  not not_3 (rsff_3_p4, RST);
  and and_17 (and_17_out, MDR[0], INSTRUCBUS[2], CPSW[6]);
  or or_2 (or_2_out, and_12_out, and_38_out);
  and and_18 (and_18_out, MDR[2], INSTRUCBUS[2]);
  and and_19 (and_19_out, MDR[3], INSTRUCBUS[2]);
  and and_20 (and_20_out, A[15], B[15], ~ALU[15]);  // AND_Gate
  or or_3 (or_3_out, and_20_out, and_21_out);
  and and_21 (and_21_out, ALU[15], ~B[15], ~A[15]);  // AND_Gate
  and and_22 (and_22_out, A[15], ~ALU[15]);  // AND_Gate
  and and_23 (and_23_out, and_22_out, INSTRUCBUS[13]);
  or or_4 (or_4_out, and_14_out, and_15_out, and_16_out);
  and and_24 (and_24_out, MDR[4], INSTRUCBUS[2]);
  and and_25 (and_25_out, ~MDR[7], INSTRUCBUS[2], CPSW[1]);  // AND_Gate
  and and_26 (and_26_out, MDR[7], INSTRUCBUS[2], CPSW[1]);
  GPR8x16 gpr8x16_1 (
    .DI15__0(mp2_16b_1_p3), .A3__0(IR19__16), .WR(CREGBUS[12]), .CLK(CLK), .DO15__0(outGPR), .RST(RST),
    .in_6(mp4_16b_2_p5), .in_7(mp4_16b_3_p5), .out_15(A), .OUTSP15__0(SP15__0),
    .OUTPC15__0({PC15__0, PC7__0}), .in_8(CREGBUS[0]), .in_9(CREGBUS[1]), .in_10(CMEMBUS[12]),
    .in_11(CMEMBUS[11]), .in_12(CMEMBUS[3]), .in_13(CMEMBUS[4]));
  and and_27 (and_27_out, ~MDR[0], INSTRUCBUS[2], CPSW[6]);  // AND_Gate
  or or_5 (or_5_out, and_27_out, CPSW[0]);
  and and_28 (and_28_out, ~or_2_out, CPSW[5]);  // AND_Gate
  and and_29 (and_29_out, CPSW[5], or_2_out);
  or or_6 (or_6_out, and_18_out, and_13_out);
  or or_7 (or_7_out, and_19_out, or_9_out);
  and and_30 (and_30_out, INSTRUCBUS[19], or_3_out);
  or or_8 (or_8_out, or_4_out, and_24_out);
  // MP4_16b mp4_16b_2: pin names not known; wires that end beside it: CREGBUS[3], CREGBUS[2], {DW15__0, DW7__0}, ALU, mp4_16b_2_p5, B, 1'b1
  not not_4 (not_4_out, RST);
  // RSFF rsff_4: pin names not known; wires that end beside it: or_5_out, CLK, and_17_out, not_4_out, PSW[0]
  // RSFF rsff_5: pin names not known; wires that end beside it: and_28_out, CLK, and_29_out, PSW[1]
  // NOT_Gate not_5 has open pins: in=RST, out=open
  and and_31 (and_31_out, ~A[0], ~A[1], ~A[2], ~A[3], ~A[4], ~A[5], ~A[6], ~A[7], ~A[8], ~A[9], ~A[10], ~A[11], ~A[12], ~A[13], ~A[14], ~A[15]);  // AND_Gate
  and and_32 (and_32_out, ~or_6_out, CPSW[4]);  // AND_Gate
  and and_33 (and_33_out, CPSW[4], or_6_out);
  and and_34 (and_34_out, ~or_7_out, CPSW[3]);  // AND_Gate
  and and_35 (and_35_out, CPSW[3], or_7_out);
  or or_9 (or_9_out, and_30_out, and_23_out);
  and and_36 (and_36_out, ~or_8_out, CPSW[2]);  // AND_Gate
  and and_37 (and_37_out, CPSW[2], or_8_out);
  or or_10 (or_10_out, and_25_out, CPSW[7]);
  or or_11 (or_11_out, CPSW[8], and_26_out);
  // RSFF rsff_6: pin names not known; wires that end beside it: CFFBUS[7], CLK, CFFBUS[6], rsff_6_p4, PHASEFFBUS[3]
  not not_6 (rsff_6_p4, RST);
  and and_38 (and_38_out, ADRINST, and_31_out);
  // RSFF rsff_7: pin names not known; wires that end beside it: and_32_out, CLK, and_33_out, rsff_7_p4, PSW[2]
  not not_7 (rsff_7_p4, RST);
  // RSFF rsff_8: pin names not known; wires that end beside it: and_34_out, CLK, and_35_out, PSW[3]
  // NOT_Gate not_8 has open pins: in=RST, out=open
  // RSFF rsff_9: pin names not known; wires that end beside it: and_36_out, CLK, and_37_out, rsff_9_p4, PSW[4]
  not not_9 (rsff_9_p4, RST);
  not not_10 (not_10_out, RST);
  // RSFF rsff_10: pin names not known; wires that end beside it: or_10_out, CLK, or_11_out, not_10_out, PSW[15]
  or or_12 (ADRINST, INSTRUCBUS[19], INSTRUCBUS[21], INSTRUCBUS[17], INSTRUCBUS[7], INSTRUCBUS[13], INSTRUCBUS[20]);
  // MP4_16b mp4_16b_3: pin names not known; wires that end beside it: CMEMBUS[14], CMEMBUS[13], addrPC, {DW15__0, DW7__0}, mp4_16b_3_p5, {IR23__16, IR19__16, IR15__8}, 1'b1

  // Other names for the same wires on the sheet: IR23__16[3:0] = IR19__16; A7__0[7:0] = A[7:0]; A15__0[15:0] = A;
  //   A15__8[7:0] = A[15:8]; immed = ADDRBUS[0]; memdir = ADDRBUS[1]; memind = ADDRBUS[2]; regind = ADDRBUS[3];
  //   regdir = ADDRBUS[4]; predec = ADDRBUS[5]; regindpom = ADDRBUS[6]; ALU15__0[15:0] = ALU; B15__0[15:0] = B;
  //   stFETCH = CFFBUS[0]; clFETCH = CFFBUS[1]; stADDR = CFFBUS[2]; clADDR = CFFBUS[3]; stEXEC = CFFBUS[4];
  //   clEXEC = CFFBUS[5]; stINTR = CFFBUS[6]; clINTR = CFFBUS[7]; ldMAR = CMEMBUS[0]; incMAR = CMEMBUS[1];
  //   ldMDR = CMEMBUS[2]; ldPC = CMEMBUS[3]; incPC = CMEMBUS[4]; mxMAR0 = CMEMBUS[5]; mxMAR1 = CMEMBUS[6];
  //   mxMAR2 = CMEMBUS[7]; mxMDR0 = CMEMBUS[8]; mxMDR1 = CMEMBUS[9]; mxMDR2 = CMEMBUS[10]; incSP = CMEMBUS[11];
  //   decSP = CMEMBUS[12]; mxPC0 = CMEMBUS[13]; mxPC1 = CMEMBUS[14]; clPSWSTART = CPSW[0]; ldI = CPSW[1];
  //   ldC = CPSW[2]; ldV = CPSW[3]; ldN = CPSW[4]; ldZ = CPSW[5]; ldSTART = CPSW[6]; clPSWI = CPSW[7];
  //   stPSWI = CPSW[8]; ldA = CREGBUS[0]; slA = CREGBUS[1]; mxA0 = CREGBUS[2]; mxA1 = CREGBUS[3];
  //   ldIR7__0 = CREGBUS[4]; ldIR15__8 = CREGBUS[5]; ldIR23__16 = CREGBUS[6]; ldIR31__24 = CREGBUS[7];
  //   ldB = CREGBUS[8]; decB = CREGBUS[9]; mxB0 = CREGBUS[10]; mxB1 = CREGBUS[11]; wrGPR = CREGBUS[12];
  //   mxGPR0 = CREGBUS[13]; ldDWL = CREGBUS[14]; ldDWH = CREGBUS[15]; ALU16 = CREGBUS[16]; Din7__0[7:0] = DIN;
  //   DW15__0[7:0] = DW7__0; DW15__8[7:0] = DW15__0; ENTRADDR15__0[15:0] = IVTPPDSP; HALT = INSTRUCBUS[0];
  //   RTS = INSTRUCBUS[1]; RTI = INSTRUCBUS[2]; INTE = INSTRUCBUS[3]; INTD = INSTRUCBUS[4]; ROL = INSTRUCBUS[5];
  //   PUSH = INSTRUCBUS[6]; POP = INSTRUCBUS[7]; BLEQ = INSTRUCBUS[8]; BNVF = INSTRUCBUS[9]; BLSSU = INSTRUCBUS[10];
  //   BOVF = INSTRUCBUS[11]; JEQL = INSTRUCBUS[12]; LOOPGRT = INSTRUCBUS[13]; BR = INSTRUCBUS[14];
  //   JMP = INSTRUCBUS[15]; JSR = INSTRUCBUS[16]; LD = INSTRUCBUS[17]; ST = INSTRUCBUS[18]; ADD = INSTRUCBUS[19];
  //   NOT = INSTRUCBUS[20]; MUL = INSTRUCBUS[21]; IR29__24[3:0] = IR27__24; IR31__24[5:0] = {IR29__24, IR27__24};
  //   MAR15__0[15:0] = MAR; MDR7__0[7:0] = MDR; PC15__0[7:0] = PC7__0; PC15__8[7:0] = PC15__0; FETCH = PHASEFFBUS[0];
  //   ADDR = PHASEFFBUS[1]; EXEC = PHASEFFBUS[2]; INTR = PHASEFFBUS[3]; PSW7__0[7:0] = PSW[7:0]; PSW15__0[15:0] = PSW;
  //   PSWSTART = PSW[0]; PSWZ = PSW[1]; PSWN = PSW[2]; PSWV = PSW[3]; PSWC = PSW[4]; PSW15__8[7:0] = PSW[15:8];
  //   PSWI = PSW[15]

  // Notes on the sheet:
  //   MAR
  //   Instrukcijski registar
  //   Dekoderi za prepoznavanje instrukcije na osnovu sadrzaja registra IR31..24
  //   MDR
  //   Pomocni registri
  //   PC
  //   FF za pokretanje FETCH, ADDR, EXEC i INTR faze izvršavanja instrukcije
  //   Programska statusna reč (PSW)
  //   Registarski fajl
endmodule

module FETCH (
  input  in_1,
  input  in_2,
  input  in_3,
  input  [3:0] PHASEFFBUS,
  input  [21:0] INSTRUCBUS,
  input  [6:0] ADDRBUS,
  input  [15:0] PSW,
  output [14:0] CMEMBUS,
  output [7:0] CFFBUS,
  output [16:0] CREGBUS,
  output rdMEM
);

  wire adr, adr2, adr3, and_3_out, bezadr, brnch2, grinst1, grinst2, jmp3, or_5_out, or_6_out, or_7_out;

  or or_1 (bezadr, INSTRUCBUS[0], INSTRUCBUS[1], INSTRUCBUS[2], INSTRUCBUS[3], INSTRUCBUS[4], INSTRUCBUS[5], INSTRUCBUS[6], INSTRUCBUS[7]);
  or or_2 (adr, INSTRUCBUS[17], INSTRUCBUS[18], INSTRUCBUS[19], INSTRUCBUS[20], INSTRUCBUS[21]);
  or or_3 (brnch2, INSTRUCBUS[8], INSTRUCBUS[9], INSTRUCBUS[10], INSTRUCBUS[11], INSTRUCBUS[14]);
  or or_4 (jmp3, INSTRUCBUS[12], INSTRUCBUS[13], INSTRUCBUS[15], INSTRUCBUS[16]);
  and and_1 (adr3, adr, ADDRBUS[6]);
  or or_5 (or_5_out, ADDRBUS[3], ADDRBUS[4], ADDRBUS[5]);
  and and_2 (adr2, or_5_out, adr);
  or or_6 (or_6_out, ADDRBUS[0], ADDRBUS[1], ADDRBUS[2], ADDRBUS[3], ADDRBUS[4], ADDRBUS[5], ADDRBUS[6]);
  and and_3 (and_3_out, INSTRUCBUS[18], ADDRBUS[0]);
  or or_7 (or_7_out, INSTRUCBUS[0], INSTRUCBUS[1], INSTRUCBUS[2], INSTRUCBUS[3], INSTRUCBUS[4], INSTRUCBUS[5], INSTRUCBUS[6], INSTRUCBUS[7], INSTRUCBUS[8], INSTRUCBUS[9], INSTRUCBUS[10], INSTRUCBUS[11], INSTRUCBUS[12], INSTRUCBUS[13], INSTRUCBUS[14], INSTRUCBUS[15], INSTRUCBUS[16], INSTRUCBUS[17], INSTRUCBUS[18], INSTRUCBUS[19], INSTRUCBUS[20], INSTRUCBUS[21]);
  not not_1 (grinst1, or_7_out);
  or or_8 (grinst2, ~or_6_out, and_3_out);  // OR_Gate

  // Other names for the same wires on the sheet: adresiranja[6:0] = ADDRBUS; immed = ADDRBUS[0]; memdir = ADDRBUS[1];
  //   memind = ADDRBUS[2]; regind = ADDRBUS[3]; predec = ADDRBUS[4]; regdir = ADDRBUS[5]; regindpom = ADDRBUS[6];
  //   CLK = in_2; FCBUS = in_3; HALT = INSTRUCBUS[0]; instrukcije[21:0] = INSTRUCBUS; RTS = INSTRUCBUS[1];
  //   RTI = INSTRUCBUS[2]; INTE = INSTRUCBUS[3]; INTD = INSTRUCBUS[4]; ROL = INSTRUCBUS[5]; PUSH = INSTRUCBUS[6];
  //   POP = INSTRUCBUS[7]; BLEQ = INSTRUCBUS[8]; BNVF = INSTRUCBUS[9]; BLSSU = INSTRUCBUS[10]; BOVF = INSTRUCBUS[11];
  //   JEQL = INSTRUCBUS[12]; LOOPGRT = INSTRUCBUS[13]; BR = INSTRUCBUS[14]; JMP = INSTRUCBUS[15];
  //   JSR = INSTRUCBUS[16]; LD = INSTRUCBUS[17]; ST = INSTRUCBUS[18]; ADD = INSTRUCBUS[19]; NOT = INSTRUCBUS[20];
  //   MUL = INSTRUCBUS[21]; FETCH = PHASEFFBUS[0]; ADDR = PHASEFFBUS[1]; EXEC = PHASEFFBUS[2]; INTR = PHASEFFBUS[3];
  //   PSWSTART = PSW[0]; rst = in_1

  // Notes on the sheet:
  //   Operaciona jedinica
  //   Kontrolna jedinica
endmodule

module ADDR (
  input  in_1,
  input  in_2,
  input  in_3,
  input  [3:0] PHASEFFBUS,
  input  [21:0] INSTRUCBUS,
  input  [6:0] ADDRBUS,
  output [14:0] CMEMBUS,
  output [7:0] CFFBUS,
  output [16:0] CREGBUS,
  output rdMEM
);


  // Other names for the same wires on the sheet: immed = ADDRBUS[0]; memdir = ADDRBUS[1]; memind = ADDRBUS[2];
  //   regind = ADDRBUS[3]; predec = ADDRBUS[4]; regdir = ADDRBUS[5]; regindpom = ADDRBUS[6]; CLK = in_2; FCBUS = in_3;
  //   rst = in_1

  // Notes on the sheet:
  //   Operaciona jedinica
  //   Upravljacka jedinica
endmodule

module EXEC (
  input  [15:0] A,
  input  in_2,
  input  in_3,
  input  in_4,
  input  [15:0] B,
  input  [3:0] PHASEFFBUS,
  input  [21:0] INSTRUCBUS,
  input  [6:0] ADDRBUS,
  input  [15:0] PSW,
  output [15:0] ALU,
  output [14:0] CMEMBUS,
  output [7:0] CFFBUS,
  output [16:0] CREGBUS,
  output [6:0] CPSW,
  output rdMEM,
  output wrMEM
);

  wire ALU16, and_1_out, and_2_out, and_3_out, and_4_out, and_5_out, and_6_out, brorjmp, or_1_out, xor_1_out;

  xor xor_1 (xor_1_out, PSW[2], PSW[3]);
  or or_1 (or_1_out, xor_1_out, PSW[1]);
  and and_1 (and_1_out, ~or_1_out, INSTRUCBUS[13]);  // AND_Gate
  and and_2 (and_2_out, or_1_out, INSTRUCBUS[8]);
  and and_3 (and_3_out, PSW[1], INSTRUCBUS[12]);
  and and_4 (and_4_out, INSTRUCBUS[10], PSW[4]);
  and and_5 (and_5_out, ~PSW[3], INSTRUCBUS[9]);  // AND_Gate
  and and_6 (and_6_out, PSW[3], INSTRUCBUS[11]);
  or or_2 (brorjmp, INSTRUCBUS[14], and_3_out, and_1_out, and_2_out, and_4_out, and_5_out, and_6_out);
  ALU16 alu16_1 (
    .A15__0(A), .B15__0(B), .ADD(INSTRUCBUS[19]), .MUL(INSTRUCBUS[21]), .DEC(INSTRUCBUS[13]),
    .NOT(INSTRUCBUS[20]), .ALU15__0(ALU), .ALU16(ALU16));

  // Other names for the same wires on the sheet: A15__0[15:0] = A; regdir = ADDRBUS[4]; ALU15__0[15:0] = ALU;
  //   B15__0[15:0] = B; CLK = in_3; FCBUS = in_4; HALT = INSTRUCBUS[0]; RTS = INSTRUCBUS[1]; RTI = INSTRUCBUS[2];
  //   INTE = INSTRUCBUS[3]; INTD = INSTRUCBUS[4]; ROL = INSTRUCBUS[5]; PUSH = INSTRUCBUS[6]; POP = INSTRUCBUS[7];
  //   BLEQ = INSTRUCBUS[8]; BNVF = INSTRUCBUS[9]; BLSSU = INSTRUCBUS[10]; BOVF = INSTRUCBUS[11];
  //   JEQL = INSTRUCBUS[12]; LOOPGRT = INSTRUCBUS[13]; BR = INSTRUCBUS[14]; JMP = INSTRUCBUS[15];
  //   JSR = INSTRUCBUS[16]; LD = INSTRUCBUS[17]; ST = INSTRUCBUS[18]; ADD = INSTRUCBUS[19]; NOT = INSTRUCBUS[20];
  //   MUL = INSTRUCBUS[21]; EXEC = PHASEFFBUS[2]; PSWZ = PSW[1]; PSWN = PSW[2]; PSWV = PSW[3]; PSWC = PSW[4];
  //   rst = in_2

  // Notes on the sheet:
  //   Operaciona jedinica
  //   Upravljacka jedinica
endmodule

module INTR (
  input  in_1,
  input  in_2,
  input  in_3,
  input  [3:0] PHASEFFBUS,
  input  [21:0] INSTRUCBUS,
  input  [15:0] PSW,
  input  [3:0] intr,
  output [15:0] ADDIVTP,
  output [2:0] UEXT1__0,
  output inta,
  output [14:0] CMEMBUS,
  output [7:0] CFFBUS,
  output [16:0] CREGBUS,
  output rdMEM,
  output wrMEM
);


  // Other names for the same wires on the sheet: ADDIVTP15__0[15:0] = ADDIVTP; CLK = in_2; FCBUS = in_3;
  //   intr3__0[3:0] = intr; ldBR = inta; rst = in_1; UEXT2__0[2:0] = UEXT1__0

  // Notes on the sheet:
  //   Operaciona jedinica
  //   Upravljacka jedinica
endmodule

module RAM (
  input  [15:0] in_1,
  input  in_2,
  input  [7:0] in_3,
  input  in_4,
  input  in_5,
  input  in_6,
  output [7:0] out_7,
  output out_8
);

  wire and_1_out, and_2_out, CNT0, LDCNT, not_1_out, notCNT0, or_1_out, reg4_ld_sl_sr_1_p6, rsff_2_p4,
       rsff_2_p5, rsff_3_p4, sl;
  wire [3:0] CNT, LFSR;

  // RSFF rsff_1: pin names not known; wires that end beside it: 1'b0, in_2, in_6, sl
  or or_1 (or_1_out, in_4, in_5);
  // REG4_LD_SL_SR reg4_ld_sl_sr_1: pin names not known; wires that end beside it: 1'b0, 1'b0, in_2, 4'b1111, LFSR, reg4_ld_sl_sr_1_p6, sl, in_6
  // RisingEdge risingedge_1: pin names not known; wires that end beside it: or_1_out, in_2, LDCNT
  // MEM64Kx8 mem64kx8_1: pin names not known; wires that end beside it: in_1, 1'b1, in_2, in_3, out_7, in_4
  xor xor_1 (reg4_ld_sl_sr_1_p6, LFSR[2], LFSR[3]);
  and and_1 (and_1_out, CNT0, not_1_out);
  not not_1 (not_1_out, LDCNT);
  // RSFF rsff_2: pin names not known; wires that end beside it: and_1_out, in_2, LDCNT, rsff_2_p4, rsff_2_p5
  not not_2 (rsff_2_p4, in_6);
  and and_2 (and_2_out, rsff_2_p5, CNT0);
  // REG4m_DEC_LD reg4m_dec_ld_1: pin names not known; wires that end beside it: in_2, LFSR, CNT, LDCNT, notCNT0, notCNT0
  or or_2 (notCNT0, CNT[0], CNT[1], CNT[2], CNT[3]);
  // RSFF rsff_3: pin names not known; wires that end beside it: out_8, in_2, and_2_out, rsff_3_p4, out_8
  not not_3 (rsff_3_p4, in_6);
  not not_4 (CNT0, notCNT0);

  // Other names for the same wires on the sheet: ADR[15:0] = in_1; CLK = in_2; DIN[7:0] = in_3; DOUT[7:0] = out_7;
  //   fc = out_8; RDMEM = in_5; rst = in_6; WRMEM = in_4

  // Notes on the sheet:
  //   Random broj predstavlja vreme pristupa memoriji
  //   Brojac za generisanje random broja 
  //   Jedinica za generisanje function complete (fc) signala
  //   Brojac za dekrementiranje random broja
endmodule
